// Logisim project 3_32206102004.circ as structural Verilog: 10 circuits, main circuit main
module main (
  input  _1,
  input  G1,
  input  in_3,
  input  in_4,
  input  A,
  input  in_6,
  input  in_7,
  input  in_8,
  input  B,
  input  in_10,
  input  in_11,
  input  in_12,
  input  in_13,
  input  in_14,
  input  \_4位数输入 ,
  input  in_16,
  input  in_17,
  input  in_18,
  input  in_19,
  input  in_20,
  input  A_2,
  input  in_22,
  input  G2AL,
  input  in_24,
  input  in_25,
  input  in_26,
  input  in_27,
  input  in_28,
  input  in_29,
  input  in_30,
  input  in_31,
  input  in_32,
  input  in_33,
  input  in_34,
  input  in_35,
  input  in_36,
  input  in_37,
  input  in_38,
  input  in_39,
  input  in_40,
  input  in_41,
  input  in_42,
  input  in_43,
  input  B_2,
  input  _00,
  input  G2BL,
  input  in_47,
  input  _01,
  input  Cin,
  input  in_50,
  input  in_51,
  input  in_52,
  input  in_53,
  input  A_3,
  input  _10,
  input  in_56,
  input  _11,
  input  in_58,
  input  B_3,
  input  in_60,
  input  Cin_2,
  input  in_62,
  input  C,
  input  in_64,
  input  in_65,
  input  in_66,
  input  in_67,
  input  in_68,
  input  G1_2,
  input  G2AL_2,
  input  G2BL_2,
  input  A_4,
  input  B_4,
  input  C_2,
  output out_75,
  output Y0L,
  output out_77,
  output out_78,
  output out_79,
  output Y1L,
  output out_81,
  output out_82,
  output out_83,
  output out_84,
  output out_85,
  output Y2L,
  output out_87,
  output Cout,
  output Y3L,
  output \确定是否存在1数量为0或3 ,
  output Y4L,
  output Y5L,
  output Y6L,
  output Y7L
);

  wire adder_1_cout, adder_2_cout, and_1_out, and_2_out, and_3_out, and_4_out, and_13_out, and_14_out,
       and_15_out, and_16_out, and_17_out, and_19_out, and_20_out, and_21_out, and_23_out, and_24_out,
       and_25_out, and_27_out, and_28_out, and_29_out, and_31_out, and_32_out, and_33_out, and_37_out,
       and_38_out, and_39_out, and_40_out, and_41_out, and_42_out, and_43_out, and_44_out, and_45_out,
       and_46_out, and_47_out, and_48_out, and_49_out, l_2_lane_selector_12f029ce_1_out_4,
       l_2_lane_selector_12f029ce_3_out_4, not_1_out, not_2_out, not_3_out, not_4_out, not_5_out, not_6_out,
       not_7_out, not_8_out, or_4_out, or_5_out, or_6_out, or_7_out, or_8_out, or_9_out, or_10_out,
       or_12_out, or_13_out, or_14_out, or_15_out, or_16_out, or_17_out, or_18_out, or_19_out, or_20_out,
       or_21_out, priority_encoder_1_gs, transistor_1_out, transistor_5_out, transistor_7_out,
       transistor_9_out, transistor_12_out, transistor_13_out, transistor_15_out, transistor_18_out,
       transistor_19_out, transistor_21_out, transistor_23_out, transistor_27_out, transistor_32_out,
       transistor_33_out, transistor_34_out, transistor_35_out, transistor_39_out, transistor_43_out,
       transistor_44_out, transistor_45_out, transistor_48_out, transistor_49_out, transistor_50_out,
       xor_1_out, xor_2_out, xor_4_out, xor_5_out, xor_6_out, xor_7_out, xor_8_out;
  wire [3:0] adder_1_out, adder_2_out, and_22_out, transistor_51_out, transistor_52_out, transistor_54_out;
  wire [3:1] not_9_out;

  and and_1 (and_1_out, _1, _1);
  or or_1 (out_75, and_1_out, and_2_out, and_3_out);
  and and_2 (and_2_out, _1, _1);
  and and_3 (and_3_out, _1, _1);
  Transistor #(.\type ("n")) transistor_1 (.in(1'b0), .out(transistor_1_out), .gate(G2AL_2));
  Transistor transistor_2 (.in(1'b1), .out(transistor_1_out), .gate(G2AL_2));
  Transistor transistor_3 (.in(1'b1), .out(transistor_1_out), .gate(G2BL_2));
  Transistor #(.\type ("n")) transistor_4 (.in(1'b0), .out(transistor_1_out), .gate(G2BL_2));
  Transistor transistor_5 (.in(1'b1), .out(transistor_5_out), .gate(A_4));
  Transistor #(.\type ("n")) transistor_6 (.in(1'b0), .out(transistor_5_out), .gate(A_4));
  Transistor transistor_7 (.in(1'b1), .out(transistor_7_out), .gate(B_4));
  Transistor #(.\type ("n")) transistor_8 (.in(1'b0), .out(transistor_7_out), .gate(B_4));
  Transistor #(.\type ("n")) transistor_9 (.in(1'b0), .out(transistor_9_out), .gate(C_2));
  Transistor transistor_10 (.in(1'b1), .out(transistor_9_out), .gate(C_2));
  Transistor transistor_11 (.in(transistor_12_out), .out(out_79), .gate(in_42));
  Transistor transistor_12 (.in(1'b0), .out(transistor_12_out), .gate(in_51));
  Transistor #(.\type ("n")) transistor_13 (.in(transistor_15_out), .out(transistor_13_out), .gate(G1_2));
  Transistor transistor_14 (.in(1'b1), .out(transistor_13_out), .gate(G1_2));
  Transistor #(.\type ("n")) transistor_15 (.in(transistor_18_out), .out(transistor_15_out), .gate(transistor_1_out));
  Transistor transistor_16 (.in(1'b1), .out(transistor_13_out), .gate(transistor_1_out));
  Transistor transistor_17 (.in(1'b1), .out(transistor_13_out), .gate(transistor_1_out));
  Transistor #(.\type ("n")) transistor_18 (.in(1'b0), .out(transistor_18_out), .gate(transistor_1_out));
  Transistor #(.\type ("n")) transistor_19 (.in(1'b0), .out(transistor_19_out), .gate(transistor_5_out));
  Transistor transistor_20 (.in(1'b1), .out(transistor_19_out), .gate(transistor_5_out));
  Transistor transistor_21 (.in(1'b1), .out(transistor_21_out), .gate(transistor_7_out));
  Transistor #(.\type ("n")) transistor_22 (.in(1'b0), .out(transistor_21_out), .gate(transistor_7_out));
  Transistor #(.\type ("n")) transistor_23 (.in(1'b0), .out(transistor_23_out), .gate(transistor_9_out));
  Transistor transistor_24 (.in(1'b1), .out(transistor_23_out), .gate(transistor_9_out));
  Transistor #(.\type ("n")) transistor_25 (.in(1'b1), .out(out_79), .gate(in_51));
  Transistor #(.\type ("n")) transistor_26 (.in(1'b1), .out(out_79), .gate(in_42));
  Transistor transistor_27 (.in(1'b1), .out(transistor_27_out), .gate(transistor_5_out));
  Transistor transistor_28 (.in(1'b1), .out(transistor_27_out), .gate(transistor_7_out));
  Transistor transistor_29 (.in(1'b1), .out(transistor_27_out), .gate(transistor_9_out));
  Transistor transistor_30 (.in(1'b1), .out(transistor_27_out), .gate(transistor_13_out));
  Transistor #(.\type ("n")) transistor_31 (.in(transistor_32_out), .out(transistor_27_out), .gate(transistor_5_out));
  Transistor #(.\type ("n")) transistor_32 (.in(transistor_33_out), .out(transistor_32_out), .gate(transistor_7_out));
  Transistor #(.\type ("n")) transistor_33 (.in(transistor_34_out), .out(transistor_33_out), .gate(transistor_9_out));
  Transistor #(.\type ("n")) transistor_34 (.in(1'b0), .out(transistor_34_out), .gate(transistor_13_out));
  Transistor transistor_35 (.in(1'b1), .out(transistor_35_out), .gate(transistor_13_out));
  Transistor transistor_36 (.in(1'b1), .out(transistor_35_out), .gate(transistor_23_out));
  Transistor transistor_37 (.in(1'b1), .out(transistor_35_out), .gate(transistor_21_out));
  Transistor transistor_38 (.in(1'b1), .out(transistor_35_out), .gate(transistor_19_out));
  xor xor_1 (xor_1_out, in_16, in_17);
  xor xor_2 (xor_2_out, in_14, \_4位数输入 );
  xor xor_3 (out_87, xor_2_out, xor_1_out);
  Transistor transistor_39 (.in(1'b1), .out(transistor_39_out), .gate(transistor_13_out));
  Transistor transistor_40 (.in(1'b1), .out(transistor_39_out), .gate(transistor_7_out));
  Transistor transistor_41 (.in(1'b1), .out(transistor_39_out), .gate(transistor_9_out));
  Transistor transistor_42 (.in(1'b1), .out(transistor_39_out), .gate(1'b0));
  Transistor #(.\type ("n")) transistor_43 (.in(1'b0), .out(transistor_43_out), .gate(transistor_13_out));
  Transistor #(.\type ("n")) transistor_44 (.in(transistor_43_out), .out(transistor_44_out), .gate(transistor_23_out));
  Transistor #(.\type ("n")) transistor_45 (.in(transistor_44_out), .out(transistor_45_out), .gate(transistor_21_out));
  Transistor #(.\type ("n")) transistor_46 (.in(transistor_45_out), .out(transistor_35_out), .gate(transistor_19_out));
  Transistor #(.\type ("n")) transistor_47 (.in(transistor_48_out), .out(transistor_39_out), .gate(transistor_13_out));
  Transistor #(.\type ("n")) transistor_48 (.in(transistor_49_out), .out(transistor_48_out), .gate(transistor_7_out));
  Transistor #(.\type ("n")) transistor_49 (.in(transistor_50_out), .out(transistor_49_out), .gate(transistor_9_out));
  Transistor #(.\type ("n")) transistor_50 (.in(1'b0), .out(transistor_50_out), .gate(1'b0));
  DotMatrix #(.inputtype("row"), .matrixcols(18), .matrixrows(8)) dotmatrix_1 (
    .row0(18'h620c), .row1(18'he612), .row2(18'h13823), .row3(18'h1840), .row4(18'h1040), .row5(18'h30c0),
    .row6(18'h16ac6), .row7(18'h18e7c));
  not not_1 (not_1_out, G1);
  and and_4 (and_4_out, ~not_1_out, ~G2AL, ~G2BL);  // AND_Gate
  not not_2 (not_2_out, A_3);
  not not_3 (not_3_out, B_3);
  not not_4 (not_4_out, C);
  not not_5 (not_5_out, not_2_out);
  not not_6 (not_6_out, not_3_out);
  not not_7 (not_7_out, not_4_out);
  and and_5 (Y0L, ~not_2_out, ~not_3_out, ~not_4_out, ~and_4_out);  // AND_Gate
  and and_6 (Y1L, ~not_5_out, ~not_3_out, ~not_4_out, ~and_4_out);  // AND_Gate
  and and_7 (Y2L, ~not_2_out, ~not_4_out, ~not_6_out, ~and_4_out);  // AND_Gate
  and and_8 (Y3L, ~not_4_out, ~not_5_out, ~not_6_out, ~and_4_out);  // AND_Gate
  and and_9 (Y4L, ~not_2_out, ~not_3_out, ~not_7_out, ~and_4_out);  // AND_Gate
  and and_10 (Y5L, ~not_3_out, ~not_5_out, ~not_7_out, ~and_4_out);  // AND_Gate
  and and_11 (Y6L, ~not_2_out, ~not_6_out, ~not_7_out, ~and_4_out);  // AND_Gate
  and and_12 (Y7L, ~and_4_out, ~not_7_out, ~not_6_out, ~not_5_out);  // AND_Gate
  // Probe on {out_82, out_83, out_84, out_85}
  Priority_Encoder #(.select(4)) priority_encoder_1 (
    .in0(in_3), .in1(in_18), .in2(in_24), .in3(in_43), .in4(in_47), .in5(in_50), .in6(in_53), .in7(in_56),
    .in8(in_58), .in9(in_60), .in10(in_62), .in11(in_64), .in12(in_65), .in13(in_66), .in14(in_67),
    .in15(in_68), .out({out_82, out_83, out_84, out_85}), .gs(priority_encoder_1_gs), .en_in(1'b1));  // open: en_out
  // Probe on {out_82, out_83, out_84, out_85}
  Hex_Digit_Display hex_digit_display_1 (.value({out_82, out_83, out_84, out_85}), .dp(priority_encoder_1_gs));
  not not_8 (not_8_out, in_4);
  and and_13 (and_13_out, not_8_out, in_41);
  and and_14 (and_14_out, in_4, in_52);
  or or_2 (out_77, and_13_out, and_14_out);
  L_2_Lane_Selector_12f029ce l_2_lane_selector_12f029ce_1 (
    .in_1(in_20), .in_2(_10), .in_3(_11), .out_4(l_2_lane_selector_12f029ce_1_out_4));
  L_2_Lane_Selector_12f029ce l_2_lane_selector_12f029ce_2 (
    .in_1(in_19), .in_2(l_2_lane_selector_12f029ce_3_out_4), .in_3(l_2_lane_selector_12f029ce_1_out_4),
    .out_4(out_81));
  L_2_Lane_Selector_12f029ce l_2_lane_selector_12f029ce_3 (
    .in_1(in_20), .in_2(_00), .in_3(_01), .out_4(l_2_lane_selector_12f029ce_3_out_4));
  and and_15 (and_15_out, B_2, A_2);
  and and_16 (and_16_out, A_2, Cin);
  and and_17 (and_17_out, Cin, B_2);
  or or_3 (out_78, and_15_out, and_16_out, and_17_out);
  ExactlyOne xor_4 (.out(xor_4_out), .in0(and_15_out), .in1(and_16_out), .in2(and_17_out));
  or or_4 (or_4_out, A_2, B_2, Cin);
  and and_18 (\确定是否存在1数量为0或3 , ~xor_4_out, or_4_out);  // AND_Gate
  and and_19 (and_19_out, in_12, in_8);
  and and_20 (and_20_out, in_8, Cin_2);
  and and_21 (and_21_out, Cin_2, in_12);
  or or_5 (or_5_out, and_19_out, and_20_out, and_21_out);
  ExactlyOne xor_5 (.out(xor_5_out), .in0(and_19_out), .in1(and_20_out), .in2(and_21_out));
  or or_6 (or_6_out, in_8, in_12, Cin_2);
  and and_22 (and_22_out[0], ~xor_5_out, or_6_out);  // AND_Gate
  and and_23 (and_23_out, in_11, in_7);
  and and_24 (and_24_out, in_7, or_5_out);
  and and_25 (and_25_out, or_5_out, in_11);
  or or_7 (or_7_out, and_23_out, and_24_out, and_25_out);
  ExactlyOne xor_6 (.out(xor_6_out), .in0(and_23_out), .in1(and_24_out), .in2(and_25_out));
  or or_8 (or_8_out, in_7, in_11, or_5_out);
  and and_26 (and_22_out[1], ~xor_6_out, or_8_out);  // AND_Gate
  and and_27 (and_27_out, in_10, in_6);
  and and_28 (and_28_out, in_6, or_7_out);
  and and_29 (and_29_out, or_7_out, in_10);
  or or_9 (or_9_out, in_6, in_10, or_7_out);
  or or_10 (or_10_out, and_27_out, and_28_out, and_29_out);
  ExactlyOne xor_7 (.out(xor_7_out), .in0(and_27_out), .in1(and_28_out), .in2(and_29_out));
  and and_30 (and_22_out[2], ~xor_7_out, or_9_out);  // AND_Gate
  and and_31 (and_31_out, B, A);
  and and_32 (and_32_out, A, or_10_out);
  and and_33 (and_33_out, or_10_out, B);
  or or_11 (Cout, and_31_out, and_32_out, and_33_out);
  ExactlyOne xor_8 (.out(xor_8_out), .in0(and_31_out), .in1(and_32_out), .in2(and_33_out));
  or or_12 (or_12_out, A, B, or_10_out);
  and and_34 (and_22_out[3], ~xor_8_out, or_12_out);  // AND_Gate
  Hex_Digit_Display hex_digit_display_2 (.value(and_22_out));  // open: dp
  and and_35 (not_9_out[3], ~transistor_51_out[2], ~transistor_51_out[1]);  // AND_Gate
  Transistor #(.\type ("n"), .gate("br"), .width(4)) transistor_51 (
    .in(adder_1_out), .out(transistor_51_out), .gate(or_13_out));
  and and_36 (not_9_out[2], transistor_51_out[2], transistor_51_out[1]);
  not not_9 (not_9_out[1], transistor_51_out[1]);
  and and_37 (and_37_out, not_9_out[3], ~not_9_out[2], not_9_out[1], ~transistor_51_out[0]);  // AND_Gate
  Transistor #(.gate("br"), .width(4)) transistor_52 (
    .in({not_9_out, transistor_51_out[0]}), .out(transistor_52_out), .gate(and_37_out));
  Transistor #(.\type ("n"), .width(4)) transistor_53 (.in(4'b0110), .out(transistor_52_out), .gate(and_37_out));
  Hex_Digit_Display hex_digit_display_3 (.value(adder_2_out));  // open: dp
  Adder #(.width(4)) adder_1 (
    .a({in_37, in_38, in_39, in_40}), .b({in_29, in_30, in_31, in_32}), .out(adder_1_out), .cout(adder_1_cout));  // open: cin
  and and_38 (and_38_out, adder_1_out[3], adder_1_out[1]);
  Adder #(.width(4)) adder_2 (
    .a({in_33, in_34, in_35, in_36}), .b({in_25, in_26, in_27, in_28}), .out(adder_2_out), .cin(or_13_out),
    .cout(adder_2_cout));
  and and_39 (and_39_out, adder_2_out[3], adder_2_out[1]);
  Hex_Digit_Display hex_digit_display_4 (.value(transistor_54_out));  // open: dp
  and and_40 (and_40_out, adder_1_out[2], adder_1_out[3]);
  or or_13 (or_13_out, or_15_out, adder_1_cout);
  and and_41 (and_41_out, adder_2_out[2], adder_2_out[3]);
  or or_14 (or_14_out, or_16_out, adder_2_cout);
  LED led_1 (.in(or_21_out));
  and and_42 (and_42_out, in_27, in_25);
  or or_15 (or_15_out, and_40_out, and_38_out);
  or or_16 (or_16_out, and_41_out, and_39_out);
  and and_43 (and_43_out, in_26, in_25);
  or or_17 (or_17_out, and_42_out, and_43_out);
  Transistor #(.width(4)) transistor_54 (.in(adder_1_out), .out(transistor_54_out), .gate(or_13_out));
  LED led_2 (.in(or_14_out));
  and and_44 (and_44_out, in_31, in_29);
  or or_18 (or_18_out, and_44_out, and_45_out);
  and and_45 (and_45_out, in_30, in_29);
  Transistor #(.\type ("n"), .width(4)) transistor_55 (
    .in(transistor_52_out), .out(transistor_54_out), .gate(or_13_out));
  and and_46 (and_46_out, in_35, in_33);
  and and_47 (and_47_out, in_34, in_33);
  or or_19 (or_19_out, and_46_out, and_47_out);
  and and_48 (and_48_out, in_39, in_37);
  or or_20 (or_20_out, and_48_out, and_49_out);
  and and_49 (and_49_out, in_38, in_37);
  or or_21 (or_21_out, or_20_out, or_19_out, or_18_out, or_17_out);
  LED led_3 ();  // open: in

  assign in_13 = _1;
  assign in_22 = _1;

  // Notes on the sheet:
  //   2.
  //   15
  //   3
  //   0为双，1为单数
  //   7
  //   14
  //   G
  //   NA
  //   NB
  //   NC
  //   Power
  //   Ground
  //   NNA
  //   NNB
  //   NNC
  //   4
  //   显示名字 𝔁𝓬 ，即徐诚的缩写
  //   5.
  //   6.
  //   7.
  //   8.
  //   确定是否存在1数量<=2
  //   串联
  //   9
  //   输入了非十进制数目
  //   输出只对有效输入负责!
  //   输出溢出
  //   溢出提示
  //   佔位符
endmodule

module L_2_Lane_Selector_12f029ce (
  input  in_1,
  input  in_2,
  input  in_3,
  output out_4
);

  wire and_1_out, and_2_out, not_1_out;

  not not_1 (not_1_out, in_1);
  and and_1 (and_1_out, not_1_out, in_2);
  and and_2 (and_2_out, in_1, in_3);
  or or_1 (out_4, and_1_out, and_2_out);
endmodule

module two (
  input  in_1,
  input  in_2,
  output out_3
);

  wire transistor_3_out;

  Transistor #(.\type ("n")) transistor_1 (.in(1'b1), .out(out_3), .gate(in_2));
  Transistor transistor_2 (.in(transistor_3_out), .out(out_3), .gate(in_1));
  Transistor transistor_3 (.in(1'b0), .out(transistor_3_out), .gate(in_2));
  Transistor #(.\type ("n")) transistor_4 (.in(1'b1), .out(out_3), .gate(in_1));
endmodule

module three (
  input  in_1,
  input  \_4位数输入 ,
  input  in_3,
  input  in_4,
  output out_5
);

  wire xor_1_out, xor_2_out;

  xor xor_1 (xor_1_out, in_1, \_4位数输入 );
  xor xor_2 (xor_2_out, in_3, in_4);
  xor xor_3 (out_5, xor_1_out, xor_2_out);

  // Notes on the sheet:
  //   3
  //   0为双，1为单数
endmodule

module four (
);

  DotMatrix #(.inputtype("row"), .matrixcols(18), .matrixrows(8)) dotmatrix_1 (
    .row0(18'h620c), .row1(18'he612), .row2(18'h13823), .row3(18'h1840), .row4(18'h1040), .row5(18'h30c0),
    .row6(18'h16ac6), .row7(18'h18e7c));

  // Notes on the sheet:
  //   显示名字 𝔁𝓬 ，即徐诚的缩写
endmodule

module five (
  input  in_1,
  input  in_2,
  input  in_3,
  input  in_4,
  input  in_5,
  input  in_6,
  output out_7,
  output out_8,
  output out_9,
  output out_10,
  output out_11,
  output out_12,
  output out_13,
  output out_14
);

  wire and_1_out, not_1_out, not_2_out, not_3_out, not_4_out, not_5_out, not_6_out, not_7_out;

  not not_1 (not_1_out, in_1);
  and and_1 (and_1_out, ~not_1_out, ~in_2, ~in_3);  // AND_Gate
  not not_2 (not_2_out, in_4);
  not not_3 (not_3_out, in_5);
  not not_4 (not_4_out, in_6);
  not not_5 (not_5_out, not_2_out);
  not not_6 (not_6_out, not_3_out);
  not not_7 (not_7_out, not_4_out);
  and and_2 (out_7, ~not_2_out, ~not_3_out, ~not_4_out, ~and_1_out);  // AND_Gate
  and and_3 (out_8, ~not_5_out, ~not_3_out, ~not_4_out, ~and_1_out);  // AND_Gate
  and and_4 (out_9, ~not_2_out, ~not_4_out, ~not_6_out, ~and_1_out);  // AND_Gate
  and and_5 (out_10, ~not_4_out, ~not_5_out, ~not_6_out, ~and_1_out);  // AND_Gate
  and and_6 (out_11, ~not_2_out, ~not_3_out, ~not_7_out, ~and_1_out);  // AND_Gate
  and and_7 (out_12, ~not_3_out, ~not_5_out, ~not_7_out, ~and_1_out);  // AND_Gate
  and and_8 (out_13, ~not_2_out, ~not_6_out, ~not_7_out, ~and_1_out);  // AND_Gate
  and and_9 (out_14, ~and_1_out, ~not_7_out, ~not_6_out, ~not_5_out);  // AND_Gate
endmodule

module six (
  input  in_1,
  input  in_2,
  input  in_3,
  input  in_4,
  input  in_5,
  input  in_6,
  input  in_7,
  input  in_8,
  input  in_9,
  input  in_10,
  input  in_11,
  input  in_12,
  input  in_13,
  input  in_14,
  input  in_15,
  input  in_16,
  output out_17,
  output out_18,
  output out_19,
  output out_20
);

  wire priority_encoder_1_gs;

  // Probe on {out_17, out_18, out_19, out_20}
  Priority_Encoder #(.select(4)) priority_encoder_1 (
    .in0(in_1), .in1(in_2), .in2(in_3), .in3(in_4), .in4(in_5), .in5(in_6), .in6(in_7), .in7(in_8),
    .in8(in_9), .in9(in_10), .in10(in_11), .in11(in_12), .in12(in_13), .in13(in_14), .in14(in_15),
    .in15(in_16), .out({out_17, out_18, out_19, out_20}), .gs(priority_encoder_1_gs), .en_in(1'b1));  // open: en_out
  // Probe on {out_17, out_18, out_19, out_20}
  Hex_Digit_Display hex_digit_display_1 (.value({out_17, out_18, out_19, out_20}), .dp(priority_encoder_1_gs));
endmodule

module c7 (
  input  in_1,
  input  in_2,
  input  in_3,
  input  in_4,
  input  _00,
  input  _01,
  input  in_7,
  input  _10,
  input  _11,
  output out_10,
  output out_11
);

  wire and_1_out, and_2_out, l_2_lane_selector_12f029ce_1_out_4, l_2_lane_selector_12f029ce_2_out_4,
       not_1_out;

  not not_1 (not_1_out, in_1);
  and and_1 (and_1_out, not_1_out, in_4);
  and and_2 (and_2_out, in_1, in_7);
  or or_1 (out_10, and_1_out, and_2_out);
  L_2_Lane_Selector_12f029ce l_2_lane_selector_12f029ce_1 (
    .in_1(in_3), .in_2(_00), .in_3(_01), .out_4(l_2_lane_selector_12f029ce_1_out_4));
  L_2_Lane_Selector_12f029ce l_2_lane_selector_12f029ce_2 (
    .in_1(in_3), .in_2(_10), .in_3(_11), .out_4(l_2_lane_selector_12f029ce_2_out_4));
  L_2_Lane_Selector_12f029ce l_2_lane_selector_12f029ce_3 (
    .in_1(in_2), .in_2(l_2_lane_selector_12f029ce_1_out_4), .in_3(l_2_lane_selector_12f029ce_2_out_4),
    .out_4(out_11));
endmodule

module c8 (
  input  A,
  input  in_2,
  input  in_3,
  input  in_4,
  input  B,
  input  in_6,
  input  in_7,
  input  in_8,
  input  in_9,
  input  in_10,
  input  in_11,
  input  in_12,
  output \确定是否存在1数量__2 ,
  output Cout,
  output out_15
);

  wire and_1_out, and_2_out, and_3_out, and_5_out, and_6_out, and_7_out, and_9_out, and_10_out, and_11_out,
       and_13_out, and_14_out, and_15_out, and_17_out, and_18_out, and_19_out, or_2_out, or_3_out, or_4_out,
       or_5_out, or_6_out, or_7_out, or_8_out, or_10_out, xor_1_out, xor_2_out, xor_3_out, xor_4_out,
       xor_5_out;
  wire [3:0] and_8_out;

  and and_1 (and_1_out, in_10, in_9);
  and and_2 (and_2_out, in_9, in_11);
  and and_3 (and_3_out, in_11, in_10);
  or or_1 (\确定是否存在1数量__2 , and_1_out, and_2_out, and_3_out);
  ExactlyOne xor_1 (.out(xor_1_out), .in0(and_1_out), .in1(and_2_out), .in2(and_3_out));
  or or_2 (or_2_out, in_9, in_10, in_11);
  and and_4 (out_15, ~xor_1_out, or_2_out);  // AND_Gate
  and and_5 (and_5_out, in_8, in_4);
  and and_6 (and_6_out, in_4, in_12);
  and and_7 (and_7_out, in_12, in_8);
  or or_3 (or_3_out, and_5_out, and_6_out, and_7_out);
  ExactlyOne xor_2 (.out(xor_2_out), .in0(and_5_out), .in1(and_6_out), .in2(and_7_out));
  or or_4 (or_4_out, in_4, in_8, in_12);
  and and_8 (and_8_out[0], ~xor_2_out, or_4_out);  // AND_Gate
  and and_9 (and_9_out, in_7, in_3);
  and and_10 (and_10_out, in_3, or_3_out);
  and and_11 (and_11_out, or_3_out, in_7);
  or or_5 (or_5_out, in_3, in_7, or_3_out);
  or or_6 (or_6_out, and_9_out, and_10_out, and_11_out);
  ExactlyOne xor_3 (.out(xor_3_out), .in0(and_9_out), .in1(and_10_out), .in2(and_11_out));
  and and_12 (and_8_out[1], ~xor_3_out, or_5_out);  // AND_Gate
  and and_13 (and_13_out, in_6, in_2);
  and and_14 (and_14_out, in_2, or_6_out);
  and and_15 (and_15_out, or_6_out, in_6);
  or or_7 (or_7_out, and_13_out, and_14_out, and_15_out);
  ExactlyOne xor_4 (.out(xor_4_out), .in0(and_13_out), .in1(and_14_out), .in2(and_15_out));
  or or_8 (or_8_out, in_2, in_6, or_6_out);
  and and_16 (and_8_out[2], ~xor_4_out, or_8_out);  // AND_Gate
  and and_17 (and_17_out, B, A);
  and and_18 (and_18_out, A, or_7_out);
  and and_19 (and_19_out, or_7_out, B);
  or or_9 (Cout, and_17_out, and_18_out, and_19_out);
  ExactlyOne xor_5 (.out(xor_5_out), .in0(and_17_out), .in1(and_18_out), .in2(and_19_out));
  or or_10 (or_10_out, A, B, or_7_out);
  and and_20 (and_8_out[3], ~xor_5_out, or_10_out);  // AND_Gate
  Hex_Digit_Display hex_digit_display_1 (.value(and_8_out));  // open: dp

  // Notes on the sheet:
  //   确定是否存在1数量为1或3
  //   串联
endmodule

module c9 (
  input  in_1,
  input  in_2,
  input  in_3,
  input  in_4,
  input  in_5,
  input  in_6,
  input  in_7,
  input  in_8,
  input  in_9,
  input  in_10,
  input  in_11,
  input  in_12,
  input  in_13,
  input  in_14,
  input  in_15,
  input  in_16,
  input  in_17,
  output out_18
);

  wire adder_1_cout, adder_2_cout, and_3_out, and_4_out, and_5_out, and_6_out, and_7_out, and_8_out,
       and_9_out, and_10_out, and_11_out, and_12_out, and_13_out, and_14_out, and_15_out, clock_1_out,
       or_1_out, or_2_out, or_3_out, or_4_out, or_5_out, or_6_out, or_7_out, or_8_out, or_9_out;
  wire [3:0] adder_1_out, adder_2_out, transistor_1_out, transistor_2_out, transistor_4_out;
  wire [3:1] not_1_out;

  Clock clock_1 (.out(clock_1_out));
  Counter counter_1 (.clr(in_17), .clk(clock_1_out), .carry(out_18));  // open: load, up, count, D, Q
  and and_1 (not_1_out[3], ~transistor_1_out[2], ~transistor_1_out[1]);  // AND_Gate
  and and_2 (not_1_out[2], transistor_1_out[2], transistor_1_out[1]);
  Transistor #(.\type ("n"), .gate("br"), .width(4)) transistor_1 (
    .in(adder_1_out), .out(transistor_1_out), .gate(or_1_out));
  not not_1 (not_1_out[1], transistor_1_out[1]);
  and and_3 (and_3_out, not_1_out[3], ~not_1_out[2], not_1_out[1], ~transistor_1_out[0]);  // AND_Gate
  Transistor #(.gate("br"), .width(4)) transistor_2 (
    .in({not_1_out, transistor_1_out[0]}), .out(transistor_2_out), .gate(and_3_out));
  Transistor #(.\type ("n"), .width(4)) transistor_3 (.in(4'b0110), .out(transistor_2_out), .gate(and_3_out));
  Counter counter_2 ();  // open: load, D, count, Q, carry, clk, clr
  Hex_Digit_Display hex_digit_display_1 (.value(adder_2_out));  // open: dp
  Adder #(.width(4)) adder_1 (
    .a({in_13, in_14, in_15, in_16}), .b({in_5, in_6, in_7, in_8}), .out(adder_1_out), .cout(adder_1_cout));  // open: cin
  and and_4 (and_4_out, adder_1_out[3], adder_1_out[1]);
  or or_1 (or_1_out, or_4_out, adder_1_cout);
  Adder #(.width(4)) adder_2 (
    .a({in_9, in_10, in_11, in_12}), .b({in_1, in_2, in_3, in_4}), .out(adder_2_out), .cin(or_1_out),
    .cout(adder_2_cout));
  and and_5 (and_5_out, adder_2_out[3], adder_2_out[1]);
  or or_2 (or_2_out, or_5_out, adder_2_cout);
  Hex_Digit_Display hex_digit_display_2 (.value(transistor_4_out));  // open: dp
  and and_6 (and_6_out, adder_1_out[2], adder_1_out[3]);
  and and_7 (and_7_out, adder_2_out[2], adder_2_out[3]);
  LED led_1 (.in(or_9_out));
  and and_8 (and_8_out, in_3, in_1);
  or or_3 (or_3_out, and_8_out, and_9_out);
  or or_4 (or_4_out, and_6_out, and_4_out);
  or or_5 (or_5_out, and_7_out, and_5_out);
  Counter #(.width(4), .max('hf)) counter_3 ();  // open: load, D, count, Q, carry, clk, clr
  LED led_2 (.in(or_2_out));
  and and_9 (and_9_out, in_2, in_1);
  Transistor #(.width(4)) transistor_4 (.in(adder_1_out), .out(transistor_4_out), .gate(or_1_out));
  and and_10 (and_10_out, in_6, in_5);
  and and_11 (and_11_out, in_7, in_5);
  or or_6 (or_6_out, and_11_out, and_10_out);
  Transistor #(.\type ("n"), .width(4)) transistor_5 (.in(transistor_2_out), .out(transistor_4_out), .gate(or_1_out));
  and and_12 (and_12_out, in_11, in_9);
  and and_13 (and_13_out, in_10, in_9);
  or or_7 (or_7_out, and_12_out, and_13_out);
  and and_14 (and_14_out, in_15, in_13);
  or or_8 (or_8_out, and_14_out, and_15_out);
  or or_9 (or_9_out, or_8_out, or_7_out, or_6_out, or_3_out);
  and and_15 (and_15_out, in_14, in_13);

  // Notes on the sheet:
  //   输入了非十进制数目
  //   输出只对有效输入负责!
  //   输出溢出
endmodule
